// Logisim project SD-Trabalho.circ as structural Verilog: 6 circuits, main circuit main
module main (
  input  data_av,
  input  [7:0] data,
  output done
);

  wire clk_out, not_1_out, rst_out, selectionsort_1_ld, selectionsort_1_sel;
  wire [4:0] selectionsort_1_current_state;
  wire [7:0] controlled_buffer_1_out, selectionsort_1_addr, selectionsort_1_data_out;

  // Probe on data
  // Probe on selectionsort_1_current_state
  Clock clk (.out(clk_out));
  Button rst (.out(rst_out));
  SelectionSort selectionsort_1 (
    .data(data), .data_in(controlled_buffer_1_out), .data_out(selectionsort_1_data_out),
    .Current_State(selectionsort_1_current_state), .done(done), .clk(clk_out), .rst(rst_out),
    .Addr(selectionsort_1_addr), .ld(selectionsort_1_ld), .sel(selectionsort_1_sel), .data_av(data_av));
  not not_1 (not_1_out, selectionsort_1_ld);
  assign controlled_buffer_1_out = not_1_out ? selectionsort_1_data_out : 8'bz;  // Controlled_Buffer controlled_buffer_1
  RAM ram_1 (
    .addr(selectionsort_1_addr), .data(controlled_buffer_1_out), .sel(selectionsort_1_sel), .clk(clk_out),
    .ld(selectionsort_1_ld));  // open: clr

  // Notes on the sheet:
  //   Notas:
  //   Addr (entrada "A" da memória) = Posição na memória do elemento que queremos
  //   data_out (saída bidirecional "D") = valor do elemento da posição Addr
  //   data_in (entrada bidirecional "D") = elemento que entra na posição da entrada Addr ("A")
endmodule

module SelectionSort (
  input  clk,
  input  rst,
  input  [7:0] data_in,
  input  [7:0] data,
  input  data_av,
  output ld,
  output sel,
  output done,
  output [7:0] data_out,
  output [7:0] Addr,
  output [4:0] Current_State
);

  wire controlpath_1_sel_addr, controlpath_1_sel_data_out, controlpath_1_sel_geral, controlpath_1_sel_ij,
       controlpath_1_sel_reg_i, controlpath_1_wrt_a, controlpath_1_wrt_aux1, controlpath_1_wrt_e,
       controlpath_1_wrt_i, controlpath_1_wrt_j, controlpath_1_wrt_o, controlpath_1_wrt_s,
       controlpath_1_wrt_se, datapath_1_dif1, datapath_1_igual2, datapath_1_maior1, datapath_1_menor1,
       datapath_1_order;

  DataPath datapath_1 (
    .wrt_i(controlpath_1_wrt_i), .wrt_j(controlpath_1_wrt_j), .wrt_e(controlpath_1_wrt_e), .clk(clk),
    .rst(rst), .sel_ij(controlpath_1_sel_ij), .menor1(datapath_1_menor1), .maior1(datapath_1_maior1),
    .sel_reg_i(controlpath_1_sel_reg_i), .dif1(datapath_1_dif1), .sel_geral(controlpath_1_sel_geral),
    .Igual2(datapath_1_igual2), .data_in(data_in), .order(datapath_1_order),
    .sel_Addr(controlpath_1_sel_addr), .sel_data_out(controlpath_1_sel_data_out), .data_out(data_out),
    .Addr(Addr), .wrt_A(controlpath_1_wrt_a), .wrt_s(controlpath_1_wrt_s), .wrt_o(controlpath_1_wrt_o),
    .wrt_aux1(controlpath_1_wrt_aux1), .wrt_se(controlpath_1_wrt_se), .data(data));  // open: dif2, Igual1
  ControlPath controlpath_1 (
    .data_av(data_av), .dif1(datapath_1_dif1), .order(datapath_1_order), .menor1(datapath_1_menor1),
    .maior1(datapath_1_maior1), .Igual2(datapath_1_igual2), .clk(clk), .rst(rst), .done(done),
    .sel_data_out(controlpath_1_sel_data_out), .sel_geral(controlpath_1_sel_geral),
    .sel_reg_i(controlpath_1_sel_reg_i), .wrt_i(controlpath_1_wrt_i), .wrt_A(controlpath_1_wrt_a),
    .wrt_s(controlpath_1_wrt_s), .wrt_o(controlpath_1_wrt_o), .wrt_e(controlpath_1_wrt_e),
    .wrt_j(controlpath_1_wrt_j), .sel_ij(controlpath_1_sel_ij), .sel(sel), .ld(ld),
    .wrt_aux1(controlpath_1_wrt_aux1), .sel_Addr(controlpath_1_sel_addr), .wrt_se(controlpath_1_wrt_se),
    .Current_State(Current_State));
endmodule

module DataPath (
  input  clk,
  input  wrt_i,
  input  wrt_s,
  input  sel_ij,
  input  rst,
  input  wrt_j,
  input  wrt_o,
  input  sel_reg_i,
  input  wrt_e,
  input  wrt_aux1,
  input  sel_geral,
  input  wrt_A,
  input  wrt_se,
  input  sel_Addr,
  input  sel_data_out,
  input  [7:0] data,
  input  [7:0] data_in,
  output [7:0] Addr,
  output maior1,
  output menor1,
  output [7:0] data_out,
  output Igual2,
  output dif2,
  output Igual1,
  output dif1,
  output order
);

  wire [6:0] adder_3_out, subtractor_1_out;
  wire [7:0] adder_1_out, adder_2_out, multiplexer_1_out, multiplexer_2_out, multiplexer_3_out,
       multiplexer_4_out, multiplexer_5_out, not_1_out, Reg_aux1_q, Reg_extrem_q, Reg_i_q, Reg_j_q,
       reg_sAddr_extrem_q, Reg_sAddr_q, Reg_Size_q;
  wire [7:1] Reg_order_q;

  Multiplexer #(.width(8), .enable("false")) multiplexer_1 (
    .in0({8{1'b0}}), .in1(adder_1_out), .out(multiplexer_1_out), .sel(sel_reg_i));
  Register Reg_Size (.D(data), .en(wrt_s), .Q(Reg_Size_q), .clk(clk), .clr(rst));
  Register Reg_order (.D(data), .en(wrt_o), .Q({Reg_order_q, order}), .clk(clk), .clr(rst));
  Register Reg_sAddr (.D(data), .en(wrt_A), .Q(Reg_sAddr_q), .clk(clk), .clr(rst));
  Register Reg_i (.D(multiplexer_1_out), .en(wrt_i), .Q(Reg_i_q), .clk(clk), .clr(rst));
  Register Reg_j (.D(adder_1_out), .en(wrt_j), .Q(Reg_j_q), .clk(clk), .clr(rst));
  Multiplexer #(.width(8), .enable("false")) multiplexer_2 (
    .in0(Reg_i_q), .in1(Reg_j_q), .out(multiplexer_2_out), .sel(sel_ij));
  Adder adder_1 (.a(multiplexer_2_out), .b(8'h1), .out(adder_1_out));  // open: cin, cout
  Register Reg_extrem (.D(multiplexer_2_out), .en(wrt_e), .Q(Reg_extrem_q), .clk(clk), .clr(rst));
  Multiplexer #(.width(8), .enable("false")) multiplexer_3 (
    .in0(adder_1_out), .in1(Reg_j_q), .out(multiplexer_3_out), .sel(sel_ij));
  Multiplexer #(.width(8), .enable("false")) multiplexer_4 (
    .in0(Reg_extrem_q), .in1(not_1_out), .out(multiplexer_4_out), .sel(sel_geral));
  assign not_1_out = ~Reg_extrem_q;  // NOT_Gate not_1, 8 bits wide
  Subtractor subtractor_1 (.a(multiplexer_3_out), .b(Reg_Size_q), .out({dif1, subtractor_1_out}));  // open: bin, bout
  Adder adder_2 (.a(Reg_sAddr_q), .b(multiplexer_2_out), .out(adder_2_out));  // open: cin, cout
  Multiplexer #(.width(8), .enable("false")) multiplexer_5 (
    .in0(Reg_sAddr_q), .in1(Reg_i_q), .out(multiplexer_5_out), .sel(sel_geral));
  Adder adder_3 (
    .a(multiplexer_4_out), .b(multiplexer_5_out), .out({dif2, adder_3_out}), .cin(sel_geral));  // open: cout
  Multiplexer #(.width(8), .enable("false")) multiplexer_6 (
    .in0(adder_2_out), .in1({dif2, adder_3_out}), .out(Addr), .sel(sel_Addr));
  nor nor_1 (Igual1, subtractor_1_out[0], subtractor_1_out[1], subtractor_1_out[2], subtractor_1_out[3], subtractor_1_out[4], subtractor_1_out[5], subtractor_1_out[6], dif1);
  nor nor_2 (Igual2, adder_3_out[0], adder_3_out[1], adder_3_out[2], adder_3_out[3], adder_3_out[4], adder_3_out[5], adder_3_out[6], dif2);
  Register Reg_aux1 (.D(data_in), .en(wrt_aux1), .Q(Reg_aux1_q), .clk(clk), .clr(rst));
  Register reg_sAddr_extrem (.D(data_in), .en(wrt_se), .Q(reg_sAddr_extrem_q), .clk(clk), .clr(rst));
  Comparator comparator_1 (.a(Reg_aux1_q), .b(reg_sAddr_extrem_q), .gt(maior1), .lt(menor1));  // open: eq
  Multiplexer #(.width(8), .enable("false")) multiplexer_7 (
    .in0(Reg_aux1_q), .in1(reg_sAddr_extrem_q), .out(data_out), .sel(sel_data_out));

  // Notes on the sheet:
  //   Clock e Reset:
  //   Writters:
  //   data_in ---> valor vindo da memória (lê da memória)
  //   data_out ---> valor que entra na memória (escreve na memória)
  //   O valor order é recebido pelo Control Path
  //   Seletores:
  //   Faz i + 1 ( sel = 0) ou j + 1 (sel = 1)
  //   e registra em j (estados distintos)
  //   Faz sAddr + i ou sAddr + j
  //   Comparação de i e size - 1: (sel/ij = 0) 
  //   Comparação de j e size: (sel/ij = 1)
  //   Comparação de (i e size - 1) ou (j e size)
  //   sAddr + j
  //   sAddr + i
  //   sAddr + extrem
  //   Faz sAddr + extrem (sel = 0)
  //   Compara i e extrem (sel = 1)
  //   B > A ( = 1) ou A > B ( = 0)
  //   B > A ( = 1) ou A > B ( = 0)
  //   Armazena sAddr, sAddr + i ou sAddr + j
  //   Compara sAddr + j e sAddr + extrem
  //   envia para sAddr[extrem]
  //   envia para sAddr[i]
endmodule

module ControlPath (
  input  data_av,
  input  clk,
  input  rst,
  input  dif1,
  input  order,
  input  menor1,
  input  maior1,
  input  Igual2,
  output done,
  output sel_data_out,
  output sel_geral,
  output sel_reg_i,
  output wrt_i,
  output wrt_A,
  output wrt_s,
  output wrt_o,
  output wrt_e,
  output wrt_j,
  output ld,
  output wrt_aux1,
  output sel,
  output sel_ij,
  output sel_Addr,
  output [4:0] Current_State,
  output wrt_se
);

  wire [4:0] nextstate_1_d0;

  NextState nextstate_1 (
    .Q4(Current_State[4]), .Q3(Current_State[3]), .Q2(Current_State[2]), .Q1(Current_State[1]),
    .Q0(Current_State[0]), .data_av(data_av), .dif1(dif1), .order(order), .menor1(menor1), .maior1(maior1),
    .Igual2(Igual2), .D4(nextstate_1_d0[4]), .D3(nextstate_1_d0[3]), .D2(nextstate_1_d0[2]),
    .D1(nextstate_1_d0[1]), .D0(nextstate_1_d0[0]));
  Register #(.width(5)) Reg_CS (.D(nextstate_1_d0), .Q(Current_State), .clk(clk), .clr(rst));  // open: en
  Output output_1 (
    .D4(Current_State[4]), .D3(Current_State[3]), .D2(Current_State[2]), .D1(Current_State[1]),
    .D0(Current_State[0]), .done(done), .sel_data_out(sel_data_out), .sel_geral(sel_geral),
    .sel_reg_i(sel_reg_i), .wrt_i(wrt_i), .wrt_A(wrt_A), .wrt_s(wrt_s), .wrt_o(wrt_o), .wrt_e(wrt_e),
    .wrt_j(wrt_j), .sel_ij(sel_ij), .sel(sel), .ld(ld), .wrt_aux1(wrt_aux1), .sel_Addr(sel_Addr),
    .wrt_se(wrt_se));

  // Notes on the sheet:
  //   Current_State: pull=up
endmodule

module NextState (
  input  Q4,
  input  Q3,
  input  Q2,
  input  Q1,
  input  Q0,
  input  data_av,
  input  dif1,
  input  order,
  input  menor1,
  input  maior1,
  input  Igual2,
  output D4,
  output D3,
  output D2,
  output D1,
  output D0
);

  wire and_1_out, and_2_out, and_3_out, and_4_out, and_5_out, and_6_out, and_7_out, and_8_out, and_9_out,
       and_10_out, and_11_out, and_12_out, and_13_out, and_14_out, and_15_out, and_16_out, and_17_out,
       and_18_out, and_19_out, and_20_out, and_21_out, and_22_out, and_23_out, and_24_out, and_25_out,
       and_26_out, and_27_out, and_28_out, and_29_out, and_30_out, and_31_out, and_32_out, and_33_out,
       not_1_out, not_2_out, not_3_out, not_4_out, not_5_out, not_6_out, not_7_out, not_8_out, not_9_out,
       not_10_out, not_11_out, not_12_out, not_13_out, not_14_out, not_15_out, not_16_out, not_17_out,
       not_18_out, not_19_out, not_20_out, not_21_out, not_22_out, not_23_out, not_24_out, not_25_out,
       not_26_out, not_27_out, not_28_out, not_29_out, not_30_out, not_31_out, not_32_out, not_33_out,
       not_34_out, not_35_out, not_36_out, not_37_out, not_38_out, not_39_out, not_40_out, not_41_out,
       not_42_out, not_43_out, not_44_out, not_45_out, not_46_out, not_47_out, not_48_out, not_49_out,
       not_50_out, not_51_out, not_52_out, not_53_out, not_54_out, not_55_out, not_56_out, not_57_out,
       not_58_out, not_59_out, not_60_out, not_61_out, not_62_out, not_63_out, not_64_out, not_65_out,
       not_66_out, not_67_out, not_68_out, not_69_out, not_70_out, not_71_out, not_72_out, not_73_out,
       not_74_out, not_75_out, not_76_out, not_77_out, not_78_out, not_79_out, not_80_out, not_81_out,
       not_82_out, not_83_out, not_84_out, not_85_out, not_86_out, not_87_out, not_88_out, not_89_out,
       not_90_out;

  not not_1 (not_1_out, Q4);
  not not_2 (not_2_out, Q3);
  not not_3 (not_3_out, Q2);
  not not_4 (not_4_out, dif1);
  not not_5 (not_5_out, Q4);
  not not_6 (not_6_out, Q1);
  not not_7 (not_7_out, Q0);
  not not_8 (not_8_out, Q4);
  not not_9 (not_9_out, Q3);
  not not_10 (not_10_out, Q2);
  not not_11 (not_11_out, Q1);
  not not_12 (not_12_out, Q0);
  not not_13 (not_13_out, Q4);
  not not_14 (not_14_out, Q0);
  not not_15 (not_15_out, dif1);
  not not_16 (not_16_out, Q4);
  not not_17 (not_17_out, Q3);
  not not_18 (not_18_out, Q4);
  not not_19 (not_19_out, Q2);
  not not_20 (not_20_out, Q0);
  not not_21 (not_21_out, Q4);
  not not_22 (not_22_out, Q0);
  not not_23 (not_23_out, Igual2);
  not not_24 (not_24_out, Q4);
  not not_25 (not_25_out, Q1);
  not not_26 (not_26_out, Q4);
  not not_27 (not_27_out, Q0);
  not not_28 (not_28_out, Q4);
  not not_29 (not_29_out, Q2);
  not not_30 (not_30_out, Q4);
  not not_31 (not_31_out, Q3);
  not not_32 (not_32_out, Q0);
  not not_33 (not_33_out, Q4);
  not not_34 (not_34_out, Q0);
  not not_35 (not_35_out, Igual2);
  not not_36 (not_36_out, Q4);
  not not_37 (not_37_out, Q1);
  not not_38 (not_38_out, Q4);
  not not_39 (not_39_out, Q0);
  not not_40 (not_40_out, Q4);
  not not_41 (not_41_out, Q2);
  not not_42 (not_42_out, Q4);
  not not_43 (not_43_out, Q1);
  not not_44 (not_44_out, Q4);
  not not_45 (not_45_out, Q2);
  not not_46 (not_46_out, data_av);
  not not_47 (not_47_out, Q4);
  not not_48 (not_48_out, Q2);
  not not_49 (not_49_out, dif1);
  not not_50 (not_50_out, Q4);
  not not_51 (not_51_out, Q0);
  not not_52 (not_52_out, Q4);
  not not_53 (not_53_out, Q1);
  not not_54 (not_54_out, Q4);
  not not_55 (not_55_out, Q2);
  not not_56 (not_56_out, Q4);
  not not_57 (not_57_out, Q0);
  not not_58 (not_58_out, Q3);
  not not_59 (not_59_out, Q2);
  not not_60 (not_60_out, Q1);
  not not_61 (not_61_out, Q4);
  not not_62 (not_62_out, Q2);
  not not_63 (not_63_out, Q0);
  not not_64 (not_64_out, Q3);
  not not_65 (not_65_out, Q2);
  not not_66 (not_66_out, Q1);
  not not_67 (not_67_out, data_av);
  not not_68 (not_68_out, Q4);
  not not_69 (not_69_out, Q3);
  not not_70 (not_70_out, Q2);
  not not_71 (not_71_out, data_av);
  not not_72 (not_72_out, Q4);
  not not_73 (not_73_out, Q1);
  not not_74 (not_74_out, Q0);
  not not_75 (not_75_out, Q4);
  not not_76 (not_76_out, Q0);
  not not_77 (not_77_out, Q4);
  not not_78 (not_78_out, Q2);
  not not_79 (not_79_out, Q1);
  not not_80 (not_80_out, order);
  not not_81 (not_81_out, maior1);
  not not_82 (not_82_out, Q4);
  not not_83 (not_83_out, Q2);
  not not_84 (not_84_out, Q1);
  not not_85 (not_85_out, menor1);
  not not_86 (not_86_out, Q3);
  not not_87 (not_87_out, Q2);
  not not_88 (not_88_out, Q1);
  and and_1 (and_1_out, not_1_out, not_2_out, not_3_out, Q1, Q0, not_4_out);
  and and_2 (and_2_out, not_5_out, Q3, Q2, not_6_out, not_7_out, Igual2);
  and and_3 (and_3_out, not_8_out, Q3, Q2, Q1, Q0);
  and and_4 (and_4_out, Q4, not_9_out, not_10_out, not_11_out, not_12_out);
  and and_5 (and_5_out, not_13_out, Q2, Q1, not_14_out, not_15_out);
  and and_6 (and_6_out, not_16_out, not_17_out, Q2, Q1, Q0);
  and and_7 (and_7_out, not_18_out, Q3, not_19_out, not_20_out);
  and and_8 (and_8_out, not_21_out, Q3, not_22_out, not_23_out);
  and and_9 (and_9_out, not_24_out, Q3, not_25_out, Q0);
  and and_10 (and_10_out, not_26_out, Q3, Q1, not_27_out);
  and and_11 (and_11_out, not_28_out, not_29_out, Q1, Q0, data_av, dif1);
  and and_12 (and_12_out, not_30_out, not_31_out, Q2, not_32_out);
  and and_13 (and_13_out, not_33_out, Q2, not_34_out, not_35_out);
  and and_14 (and_14_out, not_36_out, Q2, not_37_out, Q0);
  and and_15 (and_15_out, not_38_out, Q2, Q1, not_39_out);
  and and_16 (and_16_out, not_40_out, Q3, not_41_out, Q1, Q0);
  and and_17 (and_17_out, not_42_out, not_43_out, Q0, data_av);
  and and_18 (and_18_out, not_44_out, not_45_out, Q1, not_46_out);
  and and_19 (and_19_out, not_47_out, not_48_out, Q1, not_49_out);
  and and_20 (and_20_out, not_50_out, Q1, not_51_out, dif1);
  and and_21 (and_21_out, not_52_out, Q2, not_53_out, Q0);
  and and_22 (and_22_out, not_54_out, Q3, not_55_out, Q0);
  and and_23 (and_23_out, not_56_out, Q3, Q1, not_57_out);
  and and_24 (and_24_out, Q4, not_58_out, not_59_out, not_60_out, Q0);
  and and_25 (and_25_out, not_61_out, not_62_out, not_63_out, data_av);
  and and_26 (and_26_out, not_64_out, not_65_out, not_66_out, Q0, not_67_out);
  and and_27 (and_27_out, not_68_out, not_69_out, not_70_out, Q0, not_71_out, dif1);
  and and_28 (and_28_out, not_72_out, Q2, not_73_out, not_74_out);
  and and_29 (and_29_out, not_75_out, Q2, not_76_out, dif1);
  and and_30 (and_30_out, not_77_out, Q3, not_78_out, not_79_out, not_80_out, not_81_out);
  not not_89 (not_89_out, Q4);
  and and_31 (and_31_out, not_89_out, Q3, not_90_out);
  not not_90 (not_90_out, Q0);
  and and_32 (and_32_out, not_82_out, Q3, not_83_out, not_84_out, order, not_85_out);
  and and_33 (and_33_out, Q4, not_86_out, not_87_out, not_88_out);
  or or_1 (D4, and_1_out, and_2_out, and_3_out, and_4_out);
  or or_2 (D3, and_5_out, and_6_out, and_7_out, and_8_out, and_9_out, and_10_out);
  or or_3 (D2, and_11_out, and_12_out, and_13_out, and_14_out, and_15_out, and_16_out);
  or or_4 (D1, and_17_out, and_18_out, and_19_out, and_20_out, and_21_out, and_22_out, and_23_out, and_24_out);
  or or_5 (D0, and_25_out, and_26_out, and_27_out, and_28_out, and_29_out, and_30_out, and_31_out, and_32_out, and_33_out);
endmodule

module Output (
  input  D4,
  input  D3,
  input  D2,
  input  D1,
  input  D0,
  output done,
  output sel_data_out,
  output sel_geral,
  output sel_reg_i,
  output wrt_i,
  output wrt_A,
  output wrt_s,
  output wrt_o,
  output wrt_e,
  output wrt_j,
  output sel_ij,
  output sel,
  output ld,
  output wrt_aux1,
  output sel_Addr,
  output wrt_se
);

  wire and_1_out, and_5_out, and_6_out, and_7_out, and_8_out, and_9_out, and_10_out, and_11_out, and_12_out,
       and_13_out, and_14_out, and_15_out, and_16_out, and_17_out, and_18_out, and_19_out, and_20_out,
       and_21_out, and_22_out, and_23_out, and_24_out, and_25_out, and_26_out, and_27_out, and_28_out,
       and_29_out, not_1_out, not_2_out, not_3_out, not_4_out, not_5_out, not_6_out, not_7_out, not_8_out,
       not_9_out, not_10_out, not_11_out, not_12_out, not_13_out, not_14_out, not_15_out, not_16_out,
       not_17_out, not_18_out, not_19_out, not_20_out, not_21_out, not_22_out, not_23_out, not_24_out,
       not_25_out, not_26_out, not_27_out, not_28_out, not_29_out, not_30_out, not_31_out, not_32_out,
       not_33_out, not_34_out, not_35_out, not_36_out, not_37_out, not_38_out, not_39_out, not_40_out,
       not_41_out, not_42_out, not_43_out, not_44_out, not_45_out, not_46_out, not_47_out, not_48_out,
       not_49_out, not_50_out, not_51_out, not_52_out, not_53_out, not_54_out, not_55_out, not_56_out,
       not_57_out, not_58_out, not_59_out, not_60_out, not_61_out, not_62_out, not_63_out, not_64_out,
       not_65_out, not_66_out, not_67_out, not_68_out, not_69_out, not_70_out, not_71_out, not_72_out,
       not_73_out, not_74_out, not_75_out;

  not not_1 (not_1_out, D4);
  not not_2 (not_2_out, D3);
  not not_3 (not_3_out, D2);
  not not_4 (not_4_out, D1);
  not not_5 (not_5_out, D0);
  not not_6 (not_6_out, D3);
  not not_7 (not_7_out, D2);
  not not_8 (not_8_out, D1);
  not not_9 (not_9_out, D0);
  not not_10 (not_10_out, D4);
  not not_11 (not_11_out, D3);
  not not_12 (not_12_out, D2);
  not not_13 (not_13_out, D4);
  not not_14 (not_14_out, D1);
  not not_15 (not_15_out, D3);
  not not_16 (not_16_out, D2);
  not not_17 (not_17_out, D4);
  not not_18 (not_18_out, D0);
  not not_19 (not_19_out, D4);
  not not_20 (not_20_out, D3);
  not not_21 (not_21_out, D1);
  not not_22 (not_22_out, D0);
  not not_23 (not_23_out, D4);
  not not_24 (not_24_out, D2);
  not not_25 (not_25_out, D0);
  not not_26 (not_26_out, D3);
  not not_27 (not_27_out, D1);
  not not_28 (not_28_out, D2);
  not not_29 (not_29_out, D3);
  not not_30 (not_30_out, D0);
  not not_31 (not_31_out, D2);
  not not_32 (not_32_out, D0);
  not not_33 (not_33_out, D2);
  not not_34 (not_34_out, D3);
  not not_35 (not_35_out, D2);
  not not_36 (not_36_out, D1);
  not not_37 (not_37_out, D0);
  not not_38 (not_38_out, D0);
  not not_39 (not_39_out, D1);
  not not_40 (not_40_out, D2);
  not not_41 (not_41_out, D3);
  not not_42 (not_42_out, D4);
  not not_43 (not_43_out, D1);
  not not_44 (not_44_out, D4);
  not not_45 (not_45_out, D0);
  not not_46 (not_46_out, D4);
  not not_47 (not_47_out, D3);
  not not_48 (not_48_out, D1);
  not not_49 (not_49_out, D2);
  not not_50 (not_50_out, D0);
  not not_51 (not_51_out, D0);
  not not_52 (not_52_out, D1);
  not not_53 (not_53_out, D3);
  not not_54 (not_54_out, D1);
  not not_55 (not_55_out, D2);
  not not_56 (not_56_out, D1);
  not not_57 (not_57_out, D0);
  not not_58 (not_58_out, D0);
  not not_59 (not_59_out, D2);
  not not_60 (not_60_out, D1);
  not not_61 (not_61_out, D0);
  not not_62 (not_62_out, D0);
  not not_63 (not_63_out, D3);
  not not_64 (not_64_out, D2);
  not not_65 (not_65_out, D0);
  not not_66 (not_66_out, D3);
  not not_67 (not_67_out, D2);
  not not_68 (not_68_out, D1);
  not not_69 (not_69_out, D0);
  not not_70 (not_70_out, D4);
  not not_71 (not_71_out, D1);
  not not_72 (not_72_out, D0);
  not not_73 (not_73_out, D1);
  not not_74 (not_74_out, D2);
  not not_75 (not_75_out, D3);
  and and_1 (and_1_out, not_1_out, not_2_out, not_3_out, not_4_out, not_5_out);
  and and_2 (wrt_A, not_6_out, not_7_out, not_8_out, not_9_out, not_10_out);
  and and_3 (wrt_s, not_11_out, not_12_out, not_13_out, not_14_out, D0);
  and and_4 (wrt_o, not_15_out, not_16_out, not_17_out, D1, not_18_out);
  and and_5 (and_5_out, not_19_out, D2, not_20_out, not_21_out, not_22_out);
  and and_6 (and_6_out, not_23_out, D3, not_24_out, D1, not_25_out);
  and and_7 (and_7_out, not_26_out, D2, not_27_out, D0);
  and and_8 (and_8_out, D3, not_28_out, D1, D0);
  and and_9 (and_9_out, not_29_out, D2, D1, not_30_out);
  and and_10 (and_10_out, D3, not_31_out, D0, D1);
  and and_11 (and_11_out, D3, D1, not_32_out, not_33_out);
  and and_12 (and_12_out, not_34_out, D1, D0, D2);
  and and_13 (and_13_out, D2, D1, D0);
  and and_14 (and_14_out, D3, not_35_out, not_36_out, not_37_out);
  and and_15 (and_15_out, D4, not_38_out, not_39_out, not_40_out, not_41_out);
  and and_16 (and_16_out, not_42_out, D3, D2, not_43_out, D0);
  and and_17 (and_17_out, not_44_out, D3, D2, D1, not_45_out);
  and and_18 (and_18_out, not_46_out, D3, D2, D1, D0);
  and and_19 (and_19_out, not_47_out, D2, D1, D0);
  and and_20 (and_20_out, D3, not_48_out, not_49_out, not_50_out);
  and and_21 (and_21_out, D3, D2, not_51_out, D1);
  and and_22 (and_22_out, D3, D2, not_52_out, D0);
  and and_23 (and_23_out, not_53_out, D2, D1, D0);
  and and_24 (and_24_out, D3, D2, D0, not_54_out);
  and and_25 (and_25_out, D3, not_55_out, not_56_out, not_57_out);
  and and_26 (and_26_out, D3, D2, D1, not_58_out);
  and and_27 (and_27_out, D3, D2, D1, D0);
  and and_28 (and_28_out, D3, not_59_out, not_60_out, not_61_out);
  and and_29 (and_29_out, D3, D2, D1, not_62_out);
  and and_30 (done, D4, not_63_out, not_64_out, D1, not_65_out);
  and and_31 (sel_data_out, D4, not_66_out, not_67_out, not_68_out, not_69_out);
  and and_32 (sel_geral, not_70_out, D3, D2, not_71_out, not_72_out);
  and and_33 (sel_reg_i, D4, not_73_out, not_74_out, not_75_out, D0);
  or or_1 (wrt_i, sel_reg_i, and_1_out);
  or or_2 (wrt_e, and_5_out, and_6_out);
  or or_3 (wrt_j, and_7_out, and_8_out);
  or or_4 (sel_ij, and_9_out, and_10_out, and_11_out, and_12_out);
  or or_5 (ld, and_19_out, and_20_out, and_21_out, and_22_out);
  or or_6 (wrt_aux1, and_23_out, and_24_out);
  or or_7 (sel_Addr, and_25_out, and_26_out, and_27_out);
  or or_8 (wrt_se, and_28_out, and_29_out);
  or or_9 (sel, and_13_out, and_14_out, and_15_out, and_16_out, and_17_out, and_18_out);

  // Notes on the sheet:
  //   estado 4
  //   estado 6
  //   estado 11
  //   estado 10
  //   estado 7
  //   estado 7
  //   estado 8
  //   estado 16
  //   estado 13
  //   estado 14
  //   estado 15
  //   estado 7
  //   estado 8
  //   estado 14
  //   estado 13
  //   estado 7
  //   estado 13
  //   estado 8
  //   estado 14
  //   estado 15
  //   estado 8
  //   estado 14
endmodule
